# Fritzing sketch bipolar-stepper-driver (saved by Fritzing 0.8.7b)
circuit board: 8.46667cm x 5.64444cm
breadboards: 1

parts:
  IC1 = ULN2003A [package="DIP16 [THT]"]
  M1 = Stepper Motor - Bipolar
  Q1 = TRANSISTOR_NPN [package=to-92]
  Q2 = TRANSISTOR_NPN [package=to-92]
  R1 = Resistor [tolerance=±5% resistance=150 package=THT]
  R2 = Resistor [tolerance=±5% resistance=150 package=THT]
  R3 = Resistor [tolerance=±5% resistance=5.5k package=THT]
  R4 = Resistor [tolerance=±5% resistance=5.5k package=THT]
  Q3 = TRANSISTOR_NPN [package=to-92]
  Q4 = TRANSISTOR_NPN [package=to-92]
  R5 = Resistor [tolerance=±5% resistance=5.5k package=THT]
  R6 = Resistor [tolerance=±5% resistance=5.5k package=THT]
  R7 = Resistor [tolerance=±5% resistance=150 package=THT]
  R8 = Resistor [tolerance=±5% resistance=150 package=THT]
  part = Resistor [tolerance=±5% resistance=220 package=THT]  # not connected
  Power_plug1 = Power plug
  Componente1 = Arduino Uno (Rev3)

nets:
  N1: IC1.In_1, R1.Pin_0, Componente1.D9_PWM
  N2: IC1.In_2, R2.Pin_0, Componente1.D8
  N3: IC1.In_3, R7.Pin_1, Componente1.D11_PWM/MOSI
  N4: IC1.In_4, R8.Pin_1, Componente1.D10_PWM/SS
  GND: IC1.0V, R3.Pin_1, R4.Pin_0, R5.Pin_1, R6.Pin_0, Power_plug1.GND, Componente1.GND
  N5: IC1.Out_4, M1.D, Q4.E
  N6: IC1.Out_3, M1.B, Q3.E
  N7: IC1.Out_2, M1.C, Q2.E
  N8: IC1.Out_1, M1.A, Q1.E
  N9: Q1.B, R2.Pin_1, R4.Pin_1
  N10: Q1.C, Q2.C, Q3.C, Q4.C, Power_plug1.VCC
  N11: Q2.B, R1.Pin_1, R3.Pin_0
  N12: Q3.B, R5.Pin_0, R8.Pin_0
  N13: Q4.B, R6.Pin_1, R7.Pin_0
